# Fritzing sketch scheme (saved by Fritzing 0.9.3b)

parts:
  Часть1 = Arduino Nano (Rev3.0) (ICSP)
  DC_Mot_Enc1 = DC Motor with two-phase hall-encoder [part_number=VT-E-G25A-06-177E]
  Power_plug1 = Power plug
  D2F1 = D2F_FL_Omron_Snap_Action_Limit_Switch_with_Level
  D2F2 = D2F_FL_Omron_Snap_Action_Limit_Switch_with_Level
  Power_plug2 = Power plug
  J1 = Generic male header - 3 pins [form="♂ (male)" package=THT]
  DS1 = DS18B20 1-Wire Temperature Sensor [part_number=DS18B20]
  R1 = Resistor [tolerance=±5% resistance=4.7k package=THT]
  R2 = Resistor [tolerance=±5% resistance=10k package=THT]
  R3 = Resistor [tolerance=±5% resistance=10k package=THT]
  S1 = H-Bridge with L298N

nets (from the breadboard view):
  GND: Часть1.GND, Power_plug1.GND, Power_plug2.GND, DS1.GND, R2.Pin_1, R3.Pin_1, S1.GND
  N1: Часть1.D2, DC_Mot_Enc1.pin3
  N2: Часть1.D3, DC_Mot_Enc1.pin4
  N3: Часть1.D4, D2F1.connector1pad_1, R3.Pin_0
  N4: Часть1.D5, D2F2.connector1pad_1, R2.Pin_0
  N5: Часть1.D6, S1.ENB
  N6: Часть1.D7, S1.IN4
  N7: Часть1.D8, S1.IN3
  N8: Часть1.D9, S1.IN2
  N9: Часть1.D10, S1.IN1
  N10: Часть1.D11/MOSI, S1.ENA
  N11: Часть1.D12/MISO, DS1.DQ, R1.Pin_0
  VCC: Часть1.VIN, Power_plug1.VCC, Power_plug2.VCC, S1.12V
  5V: Часть1.5V, D2F1.connector1, D2F2.connector1, DS1.VDD, R1.Pin_1
  N12: Часть1.3V3, DC_Mot_Enc1.pin2
  N13: DC_Mot_Enc1.pin1, S1.M2-02
  N14: DC_Mot_Enc1.pin5, DC_Mot_Enc1.pin6, S1.M2-01
  N15: J1.pin1, S1.M1-01
  N16: J1.pin2, S1.M1-02

custom parts:
  Generic male header - 3 pins: Generic male header
  H-Bridge with L298N: h-bridge
